// Logisim project 4bitswap.circ as structural Verilog: 4 circuits, main circuit main
module main (
  output [3:0] A,
  output [3:0] B,
  output [3:0] C,
  output [3:0] D,
  output [3:0] out_5,
  output [3:0] out_6,
  output [3:0] out_7,
  output [3:0] out_8,
  output halt
);

  wire clock_1_out;
  wire [3:0] counter_1_q;

  Counter #(.width(4), .max('hf)) counter_1 (
    .Q(counter_1_q), .carry(halt), .clk(clock_1_out));  // open: load, D, count, clr
  Clock clock_1 (.out(clock_1_out));
  ROM #(.addrWidth(4), .dataWidth(16)) rom_1 (.addr(counter_1_q), .data({D, C, B, A}));  // open: sel
  _4bit_sort u_4bit_sort_1 (
    .in_1(A), .in_2(B), .in_3(C), .in_4(D), .out_5(out_5), .out_6(out_6), .out_7(out_7), .out_8(out_8));
endmodule

module _1bit_swap (
  input  in_1,
  input  in_2,
  input  in_3,
  output out_4,
  output out_5
);

  wire and_1_out, and_2_out, and_3_out, and_4_out, not_1_out, not_2_out, not_3_out, not_4_out, not_5_out,
       not_6_out, xor_1_out, xor_2_out, xor_3_out, xor_4_out;

  xor xor_1 (xor_1_out, in_1, not_1_out);
  not not_1 (not_1_out, in_3);
  xor xor_2 (xor_2_out, in_2, not_2_out);
  not not_2 (not_2_out, in_3);
  not not_3 (not_3_out, in_3);
  not not_4 (not_4_out, in_3);
  xor xor_3 (xor_3_out, xor_1_out, not_3_out);
  not not_5 (not_5_out, in_3);
  xor xor_4 (xor_4_out, xor_2_out, not_4_out);
  not not_6 (not_6_out, in_3);
  and and_1 (and_1_out, in_3, xor_3_out);
  and and_2 (and_2_out, xor_3_out, not_5_out);
  and and_3 (and_3_out, xor_4_out, in_3);
  and and_4 (and_4_out, xor_4_out, not_6_out);
  or or_1 (out_4, and_2_out, and_3_out);
  or or_2 (out_5, and_1_out, and_4_out);
endmodule

module _4bit_swap (
  input  [3:0] in_1,
  input  [3:0] in_2,
  input  in_3,
  output [3:0] out_4,
  output [3:0] out_5
);

  _1bit_swap _1bit_swap (.in_1(in_1[3]), .in_2(in_2[3]), .in_3(in_3), .out_4(out_4[3]), .out_5(out_5[3]));
  _1bit_swap _1bit_swap_2 (.in_1(in_1[2]), .in_2(in_2[2]), .in_3(in_3), .out_4(out_4[2]), .out_5(out_5[2]));
  _1bit_swap _1bit_swap_3 (.in_1(in_1[1]), .in_2(in_2[1]), .in_3(in_3), .out_4(out_4[1]), .out_5(out_5[1]));
  _1bit_swap _1bit_swap_4 (.in_1(in_1[0]), .in_2(in_2[0]), .in_3(in_3), .out_4(out_4[0]), .out_5(out_5[0]));
endmodule

module _4bit_sort (
  input  [3:0] in_1,
  input  [3:0] in_2,
  input  [3:0] in_3,
  input  [3:0] in_4,
  output [3:0] out_5,
  output [3:0] out_6,
  output [3:0] out_7,
  output [3:0] out_8
);

  wire and_1_out, and_2_out, and_3_out, and_4_out, and_5_out, comparator_1_gt, comparator_1_lt,
       comparator_2_gt, comparator_2_lt, comparator_3_gt, comparator_3_lt, comparator_4_gt, comparator_4_lt,
       comparator_5_gt, comparator_5_lt, not_1_out, not_2_out, not_3_out, not_4_out, not_5_out;
  wire [3:0] _4bit_swap_2_out_4, _4bit_swap_2_out_5, _4bit_swap_out_4, _4bit_swap_out_5, n4bit_swap_2_out_4,
       n4bit_swap_2_out_5;

  Comparator #(.width(5)) comparator_1 (
    .a({1'b0, in_1}), .b({1'b0, in_2}), .gt(comparator_1_gt), .lt(comparator_1_lt));  // open: eq
  not not_1 (not_1_out, comparator_1_lt);
  Comparator #(.width(5)) comparator_2 (
    .a({1'b0, in_3}), .b({1'b0, in_4}), .gt(comparator_2_gt), .lt(comparator_2_lt));  // open: eq
  not not_2 (not_2_out, comparator_2_lt);
  and and_1 (and_1_out, comparator_1_gt, not_1_out);
  and and_2 (and_2_out, comparator_2_gt, not_2_out);
  _4bit_swap _4bit_swap (
    .in_1(in_1), .in_2(in_2), .in_3(and_1_out), .out_4(_4bit_swap_out_4), .out_5(_4bit_swap_out_5));
  _4bit_swap _4bit_swap_2 (
    .in_1(in_3), .in_2(in_4), .in_3(and_2_out), .out_4(_4bit_swap_2_out_4), .out_5(_4bit_swap_2_out_5));
  Comparator #(.width(5)) comparator_3 (
    .a({1'b0, _4bit_swap_out_4}), .b({1'b0, n4bit_swap_2_out_4}), .gt(comparator_3_gt), .lt(comparator_3_lt));  // open: eq
  not not_3 (not_3_out, comparator_3_lt);
  Comparator #(.width(5)) comparator_4 (
    .a({1'b0, _4bit_swap_out_5}), .b({1'b0, _4bit_swap_2_out_4}), .gt(comparator_4_gt), .lt(comparator_4_lt));  // open: eq
  not not_4 (not_4_out, comparator_4_lt);
  Comparator #(.width(5)) comparator_5 (
    .a({1'b0, n4bit_swap_2_out_5}), .b({1'b0, _4bit_swap_2_out_5}), .gt(comparator_5_gt), .lt(comparator_5_lt));  // open: eq
  not not_5 (not_5_out, comparator_5_lt);
  and and_3 (and_3_out, comparator_3_gt, not_3_out);
  and and_4 (and_4_out, comparator_4_gt, not_4_out);
  and and_5 (and_5_out, comparator_5_gt, not_5_out);
  _4bit_swap u_4bit_swap_1 (
    .in_1(_4bit_swap_out_4), .in_2(n4bit_swap_2_out_4), .in_3(and_3_out), .out_4(out_5), .out_5(out_6));
  _4bit_swap u_4bit_swap_2 (
    .in_1(_4bit_swap_out_5), .in_2(_4bit_swap_2_out_4), .in_3(and_4_out), .out_4(n4bit_swap_2_out_4),
    .out_5(n4bit_swap_2_out_5));
  _4bit_swap u_4bit_swap_3 (
    .in_1(n4bit_swap_2_out_5), .in_2(_4bit_swap_2_out_5), .in_3(and_5_out), .out_4(out_7), .out_5(out_8));
endmodule
