// Logisim project CRC.circ as structural Verilog: 5 circuits, main circuit main
module main (
  output [7:0] A,
  output [3:0] B,
  output [10:0] C,
  output halt
);

  wire undriven;
  wire [3:0] counter_1_q;

  Counter #(.width(4), .max('hf)) counter_1 (
    .Q(counter_1_q), .carry(halt), .clk(undriven));  // open: load, D, count, clr
  Clock clock_1 ();  // open: out
  ROM #(.addrWidth(4), .dataWidth(12)) rom_1 (.addr(counter_1_q), .data({B, A}));  // open: sel
  CRC CRC (.in_1(A), .in_2(B), .out_3(C));
endmodule

module CRC (
  input  [7:0] in_1,
  input  [3:0] in_2,
  output [10:0] out_3
);

  wire [2:0] CRC_4_bit_2_output, CRC_4_bit_3_output, CRC_4_bit_4_output, CRC_4_bit_5_output, CRC_4_bit_output;
  wire [3:0] Merger_2_merge_result, Merger_3_merge_result, Merger_4_merge_result, Merger_merge_result;

  CRC_4_bit CRC_4_bit (.Num(in_1[7:4]), .Divider(in_2), .Output(CRC_4_bit_output));
  Merger Merger (.Divide_Result(CRC_4_bit_output), .New_Number(in_1[3]), .Merge_Result(Merger_merge_result));
  CRC_4_bit CRC_4_bit_2 (.Num(Merger_merge_result), .Divider(in_2), .Output(CRC_4_bit_2_output));
  Merger Merger_2 (.Divide_Result(CRC_4_bit_2_output), .New_Number(in_1[2]), .Merge_Result(Merger_2_merge_result));
  CRC_4_bit CRC_4_bit_3 (.Num(Merger_2_merge_result), .Divider(in_2), .Output(CRC_4_bit_3_output));
  Merger Merger_3 (.Divide_Result(CRC_4_bit_3_output), .New_Number(in_1[1]), .Merge_Result(Merger_3_merge_result));
  CRC_4_bit CRC_4_bit_4 (.Num(Merger_3_merge_result), .Divider(in_2), .Output(CRC_4_bit_4_output));
  Merger Merger_4 (.Divide_Result(CRC_4_bit_4_output), .New_Number(in_1[0]), .Merge_Result(Merger_4_merge_result));
  CRC_4_bit CRC_4_bit_5 (.Num(Merger_4_merge_result), .Divider(in_2), .Output(CRC_4_bit_5_output));
  Add_3_0 Add_3_0 (.in_1(CRC_4_bit_5_output), .in_2(in_2), .out_3(out_3[2:0]));

  assign out_3[10:3] = in_1;
endmodule

module CRC_4_bit (
  input  [3:0] Num,
  input  [3:0] Divider,
  output [2:0] Output
);

  wire [3:0] xor_1_out;
  wire [3:3] multiplexer_1_out;

  assign xor_1_out = Num ^ Divider;  // XOR_Gate xor_1, 4 bits wide
  Multiplexer #(.width(4)) multiplexer_1 (
    .in0(Num), .in1(xor_1_out), .out({multiplexer_1_out[3], Output}), .sel(Num[3]));  // open: en
  // Probe on multiplexer_1_out[3]
endmodule

module Merger (
  input  [2:0] Divide_Result,
  input  New_Number,
  output [3:0] Merge_Result
);


  assign Merge_Result = {Divide_Result, New_Number};
endmodule

module Add_3_0 (
  input  [2:0] in_1,
  input  [3:0] in_2,
  output [2:0] out_3
);

  wire [2:0] CRC_4_bit_2_output, CRC_4_bit_output;
  wire [3:0] Merger_2_merge_result, Merger_3_merge_result, Merger_merge_result;

  Merger Merger (.Divide_Result(in_1), .New_Number(1'b0), .Merge_Result(Merger_merge_result));
  CRC_4_bit CRC_4_bit (.Num(Merger_merge_result), .Divider(in_2), .Output(CRC_4_bit_output));
  Merger Merger_2 (.Divide_Result(CRC_4_bit_output), .New_Number(1'b0), .Merge_Result(Merger_2_merge_result));
  CRC_4_bit CRC_4_bit_2 (.Num(Merger_2_merge_result), .Divider(in_2), .Output(CRC_4_bit_2_output));
  Merger Merger_3 (.Divide_Result(CRC_4_bit_2_output), .New_Number(1'b0), .Merge_Result(Merger_3_merge_result));
  CRC_4_bit CRC_4_bit_3 (.Num(Merger_3_merge_result), .Divider(in_2), .Output(out_3));
endmodule
