// Logisim project fsm - Copy (2).circ as structural Verilog: 1 circuit, main circuit fsm
module fsm (
  input  Reset_Signal,
  input  [1:0] In,
  output out_3
);

  wire clock_1_out, multiplexer_1_out, multiplexer_2_out, multiplexer_3_out;
  wire [1:0] d_ff_1_q, d_ff_3_q, d_ff_5_q;

  Clock clock_1 (.out(clock_1_out));
  D_Flip_Flop d_ff_1 (.clk(clock_1_out), .D(In[0]), .Q(d_ff_1_q[0]), .reset(Reset_Signal));  // open: Qn, preset, en
  D_Flip_Flop d_ff_2 (.clk(clock_1_out), .D(In[1]), .Q(d_ff_1_q[1]), .reset(Reset_Signal));  // open: Qn, preset, en
  D_Flip_Flop d_ff_3 (
    .clk(clock_1_out), .D(d_ff_1_q[0]), .Q(d_ff_3_q[0]), .reset(Reset_Signal));  // open: Qn, preset, en
  D_Flip_Flop d_ff_4 (
    .clk(clock_1_out), .D(d_ff_1_q[1]), .Q(d_ff_3_q[1]), .reset(Reset_Signal));  // open: Qn, preset, en
  D_Flip_Flop d_ff_5 (
    .clk(clock_1_out), .D(d_ff_3_q[0]), .Q(d_ff_5_q[0]), .reset(Reset_Signal));  // open: Qn, preset, en
  D_Flip_Flop d_ff_6 (
    .clk(clock_1_out), .D(d_ff_3_q[1]), .Q(d_ff_5_q[1]), .reset(Reset_Signal));  // open: Qn, preset, en
  Multiplexer #(.select(2)) multiplexer_1 (
    .in0(1'b1), .in1(1'b0), .in2(1'b1), .in3(1'b0), .out(multiplexer_1_out), .sel(In));  // open: en
  Multiplexer #(.select(2)) multiplexer_2 (
    .in0(1'b1), .in1(1'b0), .in2(1'b1), .in3(1'b0), .out(multiplexer_2_out), .sel(d_ff_1_q));  // open: en
  Multiplexer #(.select(2)) multiplexer_3 (
    .in0(1'b0), .in1(1'b1), .in2(1'b0), .in3(1'b0), .out(multiplexer_3_out), .sel(d_ff_3_q));  // open: en
  and and_1 (out_3, multiplexer_1_out, multiplexer_2_out, multiplexer_3_out);
endmodule
