// Logisim project mod5.circ as structural Verilog: 2 circuits, main circuit main
module main (
  output out_1,
  output s0,
  output s1,
  output s2,
  output s3,
  output s4,
  output halt
);

  wire clock_1_out;
  wire [3:0] counter_1_q;

  Clock clock_1 (.out(clock_1_out));
  Counter #(.width(4), .max('hf)) counter_1 (
    .Q(counter_1_q), .carry(halt), .clk(clock_1_out));  // open: load, D, count, clr
  ROM #(.addrWidth(4), .dataWidth(1)) rom_1 (.addr(counter_1_q), .data(out_1));  // open: sel
  mod5 mod5_1 (.in_1(out_1), .out_2(s0), .out_3(s1), .out_4(s2), .out_5(s3), .out_6(s4));
endmodule

module mod5 (
  input  in_1,
  output out_2,
  output out_3,
  output out_4,
  output out_5,
  output out_6
);
endmodule
