// Logisim project cpu - Copy.circ as structural Verilog: 6 circuits, main circuit main
module main (
  input  Reset,
  output [31:0] out_2,
  output out_3,
  output [4:0] out_4,
  output [31:0] out_5,
  output out_6,
  output [4:0] out_7,
  output [31:0] out_8
);

  wire ALUSrc, clk, ExtOp, MemtoReg, nPC_sel, RegDst, Shift, zero;
  wire [2:0] ALUOp;
  wire [26:0] alu_1_out_5;
  wire [29:0] Shifted;
  wire [31:0] bit_extender_1_out, dm_1_rdata, grf_1_rdata1, multiplexer_3_out, multiplexer_4_out,
       shifter_1_out;
  wire [31:30] multiplexer_2_out;

  Clock clock_1 (.out(clk));
  IFU ifu_1 (.Shifted(Shifted), .IfBeq(nPC_sel), .zero(zero), .clk(clk), .reset(Reset), .opcode(out_2));
  Controller controller_1 (
    .funct(out_2[5:0]), .opcode(out_2[31:26]), .RegDst(RegDst), .ALUSrc(ALUSrc), .MemtoReg(MemtoReg),
    .RegWrite(out_3), .MemWrite(out_6), .nPC_sel(nPC_sel), .ExtOp(ExtOp), .ALUctr(ALUOp));
  Multiplexer #(.width(5)) multiplexer_1 (
    .in0(out_2[20:16]), .in1(out_2[15:11]), .out(out_4), .sel(RegDst));  // open: en
  assign bit_extender_1_out = {{16{1'b0}}, out_2[15:0]};  // Bit_Extender bit_extender_1
  GRF grf_1 (
    .Reg1(out_2[25:21]), .Reg2(out_2[20:16]), .RegAddr(out_4), .RegWrite(out_3), .RegData(out_5), .clk(clk),
    .reset(Reset), .RData1(grf_1_rdata1), .RData2(out_8));
  Shifter #(.width(32)) shifter_1 (.in(bit_extender_1_out), .\dist (5'b10000), .out(shifter_1_out));
  Multiplexer #(.width(32)) multiplexer_2 (
    .in0(bit_extender_1_out), .in1(shifter_1_out), .out({multiplexer_2_out, Shifted}), .sel(ExtOp));  // open: en
  Multiplexer #(.width(32)) multiplexer_3 (
    .in0(out_8), .in1({multiplexer_2_out, Shifted}), .out(multiplexer_3_out), .sel(ALUSrc));  // open: en
  ALU alu_1 (
    .A(grf_1_rdata1), .B(multiplexer_3_out), .ALUctr(ALUOp), .Zero(zero),
    .out_5({alu_1_out_5[26:2], out_7, alu_1_out_5[1:0]}));
  DM dm_1 (.A(out_7), .WData(out_8), .MemWrite(out_6), .clk(clk), .reset(Reset), .RData(dm_1_rdata));
  Multiplexer #(.width(32)) multiplexer_4 (
    .in0({alu_1_out_5[26:2], out_7, alu_1_out_5[1:0]}), .in1(dm_1_rdata), .out(multiplexer_4_out),
    .sel(MemtoReg));  // open: en
  Multiplexer #(.width(32)) multiplexer_5 (
    .in0(multiplexer_4_out), .in1({multiplexer_2_out, Shifted}), .out(out_5), .sel(Shift));  // open: en

  // Other names for the same wires on the sheet: MemAddr[4:0] = out_7; _5_0[5:0] = out_2[5:0];
  //   _15_0[15:0] = out_2[15:0]; Instr[31:0] = out_2; _15_11[4:0] = out_2[15:11]; _20_16[4:0] = out_2[20:16];
  //   _25_21[4:0] = out_2[25:21]; _31_26[5:0] = out_2[31:26]; MemData[31:0] = out_8; MemWrite = out_6;
  //   RegAddr[4:0] = out_4; RegData[31:0] = out_5; RegWrite = out_3
endmodule

module IFU (
  input  [29:0] Shifted,
  input  IfBeq,
  input  clk,
  input  reset,
  input  zero,
  output [31:0] opcode
);

  wire [29:0] adder_1_out, adder_2_out, multiplexer_1_out, register_1_q;
  wire [31:30] adder_2_out_2;

  Adder #(.width(30)) adder_1 (.a(adder_2_out), .b(Shifted), .out(adder_1_out));  // open: cin, cout
  Register #(.width(30)) register_1 (.D(multiplexer_1_out), .Q(register_1_q), .clk(clk), .clr(reset));  // open: en
  Multiplexer #(.select(2), .width(30)) multiplexer_1 (
    .in0(adder_2_out), .in1(adder_2_out), .in2(adder_2_out), .in3(adder_1_out), .out(multiplexer_1_out),
    .sel({zero, IfBeq}));  // open: en
  Adder #(.width(32)) adder_2 (
    .a({2'b00, register_1_q}), .b(32'h1), .out({adder_2_out_2, adder_2_out}));  // open: cin, cout
  ROM #(.addrWidth(5), .dataWidth(32)) rom_1 (.addr(register_1_q[4:0]), .data(opcode));  // open: sel

  // Notes on the sheet:
  //   contents of rom_1 (hex, n*v repeats v):
  //   34010014 3428000d 3412001e 3404000e 341c0002 341d000d 3401000c 3c010000 34210015 11021 201821
  //   3c010000 3421000c 212023 3c010000 3421000d 2413023 3c07000c ac230008 8c290008 3c010000 3421000a
  //   616021 1816021 606823 11800001 1021fff9 3c030014 3c1c0015 3c1d0023
endmodule

module ALU (
  input  [31:0] A,
  input  [31:0] B,
  input  [2:0] ALUctr,
  output Zero,
  output [31:0] out_5
);

  wire [31:0] adder_1_out, OR_out, subtractor_1_out;

  Adder #(.width(32)) adder_1 (.a(A), .b(B), .out(adder_1_out));  // open: cin, cout
  Subtractor #(.width(32)) subtractor_1 (.a(A), .b(B), .out(subtractor_1_out));  // open: bin, bout
  assign OR_out = A | B;  // OR_Gate OR, 32 bits wide
  Multiplexer #(.select(3), .width(32)) multiplexer_1 (
    .in0(B), .in1(OR_out), .in2(subtractor_1_out), .in3(adder_1_out), .out(out_5), .sel(ALUctr));  // open: in4, in5, in6, in7, en
  nor nor_1 (Zero, out_5[0], out_5[1], out_5[2], out_5[3], out_5[4], out_5[5], out_5[6], out_5[7], out_5[8], out_5[9], out_5[10], out_5[11], out_5[12], out_5[13], out_5[14], out_5[15], out_5[16], out_5[17], out_5[18], out_5[19], out_5[20], out_5[21], out_5[22], out_5[23], out_5[24], out_5[25], out_5[26], out_5[27], out_5[28], out_5[29], out_5[30], out_5[31]);
endmodule

module Controller (
  input  [5:0] opcode,
  input  [5:0] funct,
  output RegDst,
  output ALUSrc,
  output MemtoReg,
  output RegWrite,
  output MemWrite,
  output nPC_sel,
  output ExtOp,
  output [2:0] ALUctr
);

  wire addu, beq, lui, lw, not_1_out, not_2_out, not_3_out, not_4_out, not_5_out, not_6_out, not_7_out,
       not_8_out, not_9_out, not_10_out, not_11_out, not_12_out, not_13_out, not_14_out, not_15_out,
       not_16_out, not_17_out, not_18_out, not_19_out, not_20_out, not_21_out, not_22_out, not_23_out,
       not_24_out, not_25_out, not_26_out, not_27_out, not_28_out, not_29_out, not_30_out, not_31_out,
       not_32_out, not_33_out, not_34_out, subu, sw;

  not not_1 (not_1_out, opcode[5]);
  not not_2 (not_2_out, opcode[4]);
  and ori (ALUctr[0], not_1_out, not_2_out, opcode[3], opcode[2], not_3_out, opcode[0]);
  not not_3 (not_3_out, opcode[1]);
  not not_4 (not_4_out, opcode[4]);
  not not_5 (not_5_out, opcode[3]);
  and u_lw (lw, opcode[5], not_4_out, not_5_out, not_6_out, opcode[1], opcode[0]);
  not not_6 (not_6_out, opcode[2]);
  not not_7 (not_7_out, opcode[4]);
  and u_sw (sw, opcode[5], not_7_out, opcode[3], not_8_out, opcode[1], opcode[0]);
  not not_8 (not_8_out, opcode[2]);
  not not_9 (not_9_out, opcode[5]);
  not not_10 (not_10_out, opcode[4]);
  not not_11 (not_11_out, opcode[3]);
  and u_beq (beq, not_9_out, not_10_out, not_11_out, opcode[2], not_12_out, not_13_out);
  not not_12 (not_12_out, opcode[1]);
  not not_13 (not_13_out, opcode[0]);
  not not_14 (not_14_out, opcode[5]);
  not not_15 (not_15_out, opcode[4]);
  and u_lui (lui, not_14_out, not_15_out, opcode[3], opcode[2], opcode[1], opcode[0]);
  not not_16 (not_16_out, opcode[5]);
  not not_17 (not_17_out, opcode[4]);
  not not_18 (not_18_out, opcode[3]);
  not not_19 (not_19_out, opcode[2]);
  not not_20 (not_20_out, opcode[1]);
  not not_21 (not_21_out, opcode[0]);
  and u_addu (addu, not_16_out, not_17_out, not_18_out, not_19_out, not_20_out, not_21_out, funct[5], not_22_out, not_23_out, not_24_out, not_25_out, funct[0]);
  not not_22 (not_22_out, funct[4]);
  not not_23 (not_23_out, funct[3]);
  not not_24 (not_24_out, funct[2]);
  not not_25 (not_25_out, funct[1]);
  not not_26 (not_26_out, opcode[5]);
  not not_27 (not_27_out, opcode[4]);
  not not_28 (not_28_out, opcode[3]);
  not not_29 (not_29_out, opcode[2]);
  not not_30 (not_30_out, opcode[1]);
  not not_31 (not_31_out, opcode[0]);
  and u_subu (subu, not_26_out, not_27_out, not_28_out, not_29_out, not_30_out, not_31_out, funct[5], not_32_out, not_33_out, not_34_out, funct[1], funct[0]);
  not not_32 (not_32_out, funct[4]);
  not not_33 (not_33_out, funct[3]);
  not not_34 (not_34_out, funct[2]);
  or u_RegDst (RegDst, addu, subu);
  or u_ALUSrc (ALUSrc, ALUctr[0], lw, sw);
  buf u_MemtoReg (MemtoReg, lw);  // OR_Gate
  or u_RegWrite (RegWrite, lui, ALUctr[0], lw, addu, subu);
  buf u_MemWrite (MemWrite, sw);  // OR_Gate
  buf u_nPC_sel (nPC_sel, beq);  // OR_Gate
  buf u_ExtOp (ExtOp, ALUctr[0]);  // OR_Gate
  or or_1 (ALUctr[1], lw, sw, beq, addu, subu);
  or or_2 (ALUctr[2], beq, subu);

  // Other names for the same wires on the sheet: ori = ALUctr[0]
endmodule

module GRF (
  input  clk,
  input  reset,
  input  [4:0] Reg1,
  input  [4:0] Reg2,
  input  [4:0] RegAddr,
  input  RegWrite,
  input  [31:0] RegData,
  output [31:0] RData1,
  output [31:0] RData2
);

  wire _1en, _2en, _3en, _4en, _5en, _6en, _7en, _8en, _9en, _10en, _11en, _12en, _13en, _14en, _15en, _16en,
       _17en, _18en, _19en, _20en, _21en, _22en, _23en, _24en, _25en, _26en, _27en, _28en, _29en, _30en,
       _31en;
  wire [0:0] and_1_out;
  wire [31:0] _0, _1, _2, _3, _4, _5, _6, _7, _8, _9, _10, _11, _12, _13, _14, _15, _16, _17, _18, _19, _20,
       _21, _22, _23, _24, _25, _26, _27, _28, _29, _30, _31, decoder_1_out0, multiplexer_1_out;

  Decoder #(.select(5)) decoder_1 (
    .out0(decoder_1_out0[0]), .out1(decoder_1_out0[1]), .out2(decoder_1_out0[2]), .out3(decoder_1_out0[3]),
    .out4(decoder_1_out0[4]), .out5(decoder_1_out0[5]), .out6(decoder_1_out0[6]), .out7(decoder_1_out0[7]),
    .out8(decoder_1_out0[8]), .out9(decoder_1_out0[9]), .out10(decoder_1_out0[10]),
    .out11(decoder_1_out0[11]), .out12(decoder_1_out0[12]), .out13(decoder_1_out0[13]),
    .out14(decoder_1_out0[14]), .out15(decoder_1_out0[15]), .out16(decoder_1_out0[16]),
    .out17(decoder_1_out0[17]), .out18(decoder_1_out0[18]), .out19(decoder_1_out0[19]),
    .out20(decoder_1_out0[20]), .out21(decoder_1_out0[21]), .out22(decoder_1_out0[22]),
    .out23(decoder_1_out0[23]), .out24(decoder_1_out0[24]), .out25(decoder_1_out0[25]),
    .out26(decoder_1_out0[26]), .out27(decoder_1_out0[27]), .out28(decoder_1_out0[28]),
    .out29(decoder_1_out0[29]), .out30(decoder_1_out0[30]), .out31(decoder_1_out0[31]), .sel(RegAddr));  // open: en
  Multiplexer #(.width(32)) multiplexer_1 (
    .in0({32{1'b0}}), .in1({32{1'b1}}), .out(multiplexer_1_out), .sel(RegWrite));  // open: en
  assign {_31en, _30en, _29en, _28en, _27en, _26en, _25en, _24en, _23en, _22en, _21en, _20en, _19en, _18en, _17en, _16en, _15en, _14en, _13en, _12en, _11en, _10en, _9en, _8en, _7en, _6en, _5en, _4en, _3en, _2en, _1en, and_1_out[0]} = decoder_1_out0 & multiplexer_1_out;  // AND_Gate and_1, 32 bits wide
  Register #(.width(32)) register_1 (.D(RegData), .en(1'b0), .Q(_0), .clk(clk), .clr(reset));
  Register #(.width(32)) register_2 (.D(RegData), .en(_1en), .Q(_1), .clk(clk), .clr(reset));
  Register #(.width(32)) register_3 (.D(RegData), .en(_2en), .Q(_2), .clk(clk), .clr(reset));
  Register #(.width(32)) register_4 (.D(RegData), .en(_3en), .Q(_3), .clk(clk), .clr(reset));
  Register #(.width(32)) register_5 (.D(RegData), .en(_4en), .Q(_4), .clk(clk), .clr(reset));
  Register #(.width(32)) register_6 (.D(RegData), .en(_5en), .Q(_5), .clk(clk), .clr(reset));
  Register #(.width(32)) register_7 (.D(RegData), .en(_6en), .Q(_6), .clk(clk), .clr(reset));
  Register #(.width(32)) register_8 (.D(RegData), .en(_7en), .Q(_7), .clk(clk), .clr(reset));
  Register #(.width(32)) register_9 (.D(RegData), .en(_8en), .Q(_8), .clk(clk), .clr(reset));
  Register #(.width(32)) register_10 (.D(RegData), .en(_9en), .Q(_9), .clk(clk), .clr(reset));
  Register #(.width(32)) register_11 (.D(RegData), .en(_10en), .Q(_10), .clk(clk), .clr(reset));
  Register #(.width(32)) register_12 (.D(RegData), .en(_11en), .Q(_11), .clk(clk), .clr(reset));
  Register #(.width(32)) register_13 (.D(RegData), .en(_12en), .Q(_12), .clk(clk), .clr(reset));
  Register #(.width(32)) register_14 (.D(RegData), .en(_13en), .Q(_13), .clk(clk), .clr(reset));
  Register #(.width(32)) register_15 (.D(RegData), .en(_14en), .Q(_14), .clk(clk), .clr(reset));
  Register #(.width(32)) register_16 (.D(RegData), .en(_15en), .Q(_15), .clk(clk), .clr(reset));
  Register #(.width(32)) register_17 (.D(RegData), .en(_16en), .Q(_16), .clk(clk), .clr(reset));
  Register #(.width(32)) register_18 (.D(RegData), .en(_17en), .Q(_17), .clk(clk), .clr(reset));
  Register #(.width(32)) register_19 (.D(RegData), .en(_18en), .Q(_18), .clk(clk), .clr(reset));
  Register #(.width(32)) register_20 (.D(RegData), .en(_19en), .Q(_19), .clk(clk), .clr(reset));
  Register #(.width(32)) register_21 (.D(RegData), .en(_20en), .Q(_20), .clk(clk), .clr(reset));
  Register #(.width(32)) register_22 (.D(RegData), .en(_21en), .Q(_21), .clk(clk), .clr(reset));
  Register #(.width(32)) register_23 (.D(RegData), .en(_22en), .Q(_22), .clk(clk), .clr(reset));
  Register #(.width(32)) register_24 (.D(RegData), .en(_23en), .Q(_23), .clk(clk), .clr(reset));
  Register #(.width(32)) register_25 (.D(RegData), .en(_24en), .Q(_24), .clk(clk), .clr(reset));
  Register #(.width(32)) register_26 (.D(RegData), .en(_25en), .Q(_25), .clk(clk), .clr(reset));
  Register #(.width(32)) register_27 (.D(RegData), .en(_26en), .Q(_26), .clk(clk), .clr(reset));
  Register #(.width(32)) register_28 (.D(RegData), .en(_27en), .Q(_27), .clk(clk), .clr(reset));
  Register #(.width(32)) register_29 (.D(RegData), .en(_28en), .Q(_28), .clk(clk), .clr(reset));
  Register #(.width(32)) register_30 (.D(RegData), .en(_29en), .Q(_29), .clk(clk), .clr(reset));
  Register #(.width(32)) register_31 (.D(RegData), .en(_30en), .Q(_30), .clk(clk), .clr(reset));
  Register #(.width(32)) register_32 (.D(RegData), .en(_31en), .Q(_31), .clk(clk), .clr(reset));
  Multiplexer #(.select(5), .width(32), .enable("false")) multiplexer_2 (
    .in0(_0), .in1(_1), .in2(_2), .in3(_3), .in4(_4), .in5(_5), .in6(_6), .in7(_7), .in8(_8), .in9(_9),
    .in10(_10), .in11(_11), .in12(_12), .in13(_13), .in14(_14), .in15(_15), .in16(_16), .in17(_17),
    .in18(_18), .in19(_19), .in20(_20), .in21(_21), .in22(_22), .in23(_23), .in24(_24), .in25(_25),
    .in26(_26), .in27(_27), .in28(_28), .in29(_29), .in30(_30), .in31(_31), .out(RData1), .sel(Reg1));
  Multiplexer #(.select(5), .width(32), .enable("false")) multiplexer_3 (
    .in0(_0), .in1(_1), .in2(_2), .in3(_3), .in4(_4), .in5(_5), .in6(_6), .in7(_7), .in8(_8), .in9(_9),
    .in10(_10), .in11(_11), .in12(_12), .in13(_13), .in14(_14), .in15(_15), .in16(_16), .in17(_17),
    .in18(_18), .in19(_19), .in20(_20), .in21(_21), .in22(_22), .in23(_23), .in24(_24), .in25(_25),
    .in26(_26), .in27(_27), .in28(_28), .in29(_29), .in30(_30), .in31(_31), .out(RData2), .sel(Reg2));

  // Other names for the same wires on the sheet: RD[31:0] = RegData; res = reset
endmodule

module DM (
  input  [4:0] A,
  input  [31:0] WData,
  input  MemWrite,
  input  clk,
  input  reset,
  output [31:0] RData
);

  RAM #(.addrWidth(5), .dataWidth(32), .bus("separate")) ram_1 (
    .addr(A), .din(WData), .data(RData), .str(MemWrite), .clk(clk), .clr(reset));  // open: sel, ld
endmodule
