// Logisim project fsm.circ as structural Verilog: 1 circuit, main circuit fsm
module fsm (
  input  Reset_Signal,
  input  [1:0] In,
  output out_3
);

  wire and_1_out, clock_1_out, d_ff_1_q, multiplexer_2_out, multiplexer_3_out, multiplexer_4_out;
  wire [1:0] d_ff_2_q, d_ff_4_q, multiplexer_1_out;

  Multiplexer #(.width(2)) multiplexer_1 (
    .in0(In), .in1(2'b00), .out(multiplexer_1_out), .sel(Reset_Signal));  // open: en
  and and_1 (and_1_out, d_ff_1_q, Reset_Signal);
  Clock clock_1 (.out(clock_1_out));
  D_Flip_Flop d_ff_1 (.clk(clock_1_out), .D(Reset_Signal), .Q(d_ff_1_q));  // open: Qn, preset, en, reset
  D_Flip_Flop d_ff_2 (
    .clk(clock_1_out), .D(multiplexer_1_out[0]), .Q(d_ff_2_q[0]), .reset(and_1_out));  // open: Qn, preset, en
  D_Flip_Flop d_ff_3 (
    .clk(clock_1_out), .D(multiplexer_1_out[1]), .Q(d_ff_2_q[1]), .reset(and_1_out));  // open: Qn, preset, en
  D_Flip_Flop d_ff_4 (.clk(clock_1_out), .D(d_ff_2_q[0]), .Q(d_ff_4_q[0]), .reset(and_1_out));  // open: Qn, preset, en
  D_Flip_Flop d_ff_5 (.clk(clock_1_out), .D(d_ff_2_q[1]), .Q(d_ff_4_q[1]), .reset(and_1_out));  // open: Qn, preset, en
  Multiplexer #(.select(2)) multiplexer_2 (
    .in0(1'b1), .in1(1'b0), .in2(1'b1), .in3(1'b0), .out(multiplexer_2_out), .sel(multiplexer_1_out));  // open: en
  Multiplexer #(.select(2)) multiplexer_3 (
    .in0(1'b1), .in1(1'b0), .in2(1'b1), .in3(1'b0), .out(multiplexer_3_out), .sel(d_ff_2_q));  // open: en
  Multiplexer #(.select(2)) multiplexer_4 (
    .in0(1'b0), .in1(1'b1), .in2(1'b0), .in3(1'b0), .out(multiplexer_4_out), .sel(d_ff_4_q));  // open: en
  and and_2 (out_3, multiplexer_2_out, multiplexer_3_out, multiplexer_4_out);
endmodule
