// Logisim project grf.circ as structural Verilog: 2 circuits, main circuit main
module main (
  output [31:0] RD1,
  output [31:0] RD2,
  output out_3
);

  wire clock_1_out;
  wire [7:0] counter_1_q;
  wire [31:0] rom_1_data, rom_2_data;

  Clock clock_1 (.out(clock_1_out));
  Counter counter_1 (.Q(counter_1_q), .carry(out_3), .clk(clock_1_out));  // open: load, D, count, clr
  ROM #(.dataWidth(32)) rom_1 (.addr(counter_1_q), .data(rom_1_data));  // open: sel
  ROM #(.dataWidth(32)) rom_2 (.addr(counter_1_q), .data(rom_2_data));  // open: sel
  grf grf_1 (
    .A1(rom_1_data[14:10]), .A2(rom_1_data[9:5]), .A3(rom_1_data[4:0]), .WD(rom_2_data), .clock(clock_1_out),
    .reset(rom_1_data[16]), .WE(rom_1_data[15]), .RD1(RD1), .RD2(RD2));

  // Notes on the sheet:
  //   reset
  //   WE
  //   A1
  //   A2
  //   A3
  //   WD
endmodule

module grf (
  input  clock,
  input  reset,
  input  WE,
  input  [4:0] A1,
  input  [4:0] A2,
  input  [4:0] A3,
  input  [31:0] WD,
  output [31:0] RD1,
  output [31:0] RD2
);

  wire _1en, _2en, _3en, _4en, _5en, _6en, _7en, _8en, _9en, _10en, _11en, _12en, _13en, _14en, _15en, _16en,
       _17en, _18en, _19en, _20en, _21en, _22en, _23en, _24en, _25en, _26en, _27en, _28en, _29en, _30en,
       _31en;
  wire [0:0] and_1_out;
  wire [31:0] _0, _1, _2, _3, _4, _5, _6, _7, _8, _9, _10, _11, _12, _13, _14, _15, _16, _17, _18, _19, _20,
       _21, _22, _23, _24, _25, _26, _27, _28, _29, _30, _31, decoder_1_out0, multiplexer_1_out;

  Decoder #(.select(5), .disabled(0)) decoder_1 (
    .out0(decoder_1_out0[0]), .out1(decoder_1_out0[1]), .out2(decoder_1_out0[2]), .out3(decoder_1_out0[3]),
    .out4(decoder_1_out0[4]), .out5(decoder_1_out0[5]), .out6(decoder_1_out0[6]), .out7(decoder_1_out0[7]),
    .out8(decoder_1_out0[8]), .out9(decoder_1_out0[9]), .out10(decoder_1_out0[10]),
    .out11(decoder_1_out0[11]), .out12(decoder_1_out0[12]), .out13(decoder_1_out0[13]),
    .out14(decoder_1_out0[14]), .out15(decoder_1_out0[15]), .out16(decoder_1_out0[16]),
    .out17(decoder_1_out0[17]), .out18(decoder_1_out0[18]), .out19(decoder_1_out0[19]),
    .out20(decoder_1_out0[20]), .out21(decoder_1_out0[21]), .out22(decoder_1_out0[22]),
    .out23(decoder_1_out0[23]), .out24(decoder_1_out0[24]), .out25(decoder_1_out0[25]),
    .out26(decoder_1_out0[26]), .out27(decoder_1_out0[27]), .out28(decoder_1_out0[28]),
    .out29(decoder_1_out0[29]), .out30(decoder_1_out0[30]), .out31(decoder_1_out0[31]), .sel(A3));  // open: en
  Multiplexer #(.width(32)) multiplexer_1 (
    .in0({32{1'b0}}), .in1({32{1'b1}}), .out(multiplexer_1_out), .sel(WE));  // open: en
  assign {_31en, _30en, _29en, _28en, _27en, _26en, _25en, _24en, _23en, _22en, _21en, _20en, _19en, _18en, _17en, _16en, _15en, _14en, _13en, _12en, _11en, _10en, _9en, _8en, _7en, _6en, _5en, _4en, _3en, _2en, _1en, and_1_out[0]} = decoder_1_out0 & multiplexer_1_out;  // AND_Gate and_1, 32 bits wide
  Register #(.width(32)) u__0 (.D(WD), .en(1'b0), .Q(_0), .clk(clock), .clr(reset));
  Register #(.width(32)) u__1 (.D(WD), .en(_1en), .Q(_1), .clk(clock), .clr(reset));
  Register #(.width(32)) u__2 (.D(WD), .en(_2en), .Q(_2), .clk(clock), .clr(reset));
  Register #(.width(32)) u__3 (.D(WD), .en(_3en), .Q(_3), .clk(clock), .clr(reset));
  Register #(.width(32)) u__4 (.D(WD), .en(_4en), .Q(_4), .clk(clock), .clr(reset));
  Register #(.width(32)) u__5 (.D(WD), .en(_5en), .Q(_5), .clk(clock), .clr(reset));
  Register #(.width(32)) u__6 (.D(WD), .en(_6en), .Q(_6), .clk(clock), .clr(reset));
  Register #(.width(32)) u__7 (.D(WD), .en(_7en), .Q(_7), .clk(clock), .clr(reset));
  Register #(.width(32)) u__8 (.D(WD), .en(_8en), .Q(_8), .clk(clock), .clr(reset));
  Register #(.width(32)) u__9 (.D(WD), .en(_9en), .Q(_9), .clk(clock), .clr(reset));
  Register #(.width(32)) u__10 (.D(WD), .en(_10en), .Q(_10), .clk(clock), .clr(reset));
  Register #(.width(32)) u__11 (.D(WD), .en(_11en), .Q(_11), .clk(clock), .clr(reset));
  Register #(.width(32)) u__12 (.D(WD), .en(_12en), .Q(_12), .clk(clock), .clr(reset));
  Register #(.width(32)) u__13 (.D(WD), .en(_13en), .Q(_13), .clk(clock), .clr(reset));
  Register #(.width(32)) u__14 (.D(WD), .en(_14en), .Q(_14), .clk(clock), .clr(reset));
  Register #(.width(32)) u__15 (.D(WD), .en(_15en), .Q(_15), .clk(clock), .clr(reset));
  Register #(.width(32)) u__16 (.D(WD), .en(_16en), .Q(_16), .clk(clock), .clr(reset));
  Register #(.width(32)) u__17 (.D(WD), .en(_17en), .Q(_17), .clk(clock), .clr(reset));
  Register #(.width(32)) u__18 (.D(WD), .en(_18en), .Q(_18), .clk(clock), .clr(reset));
  Register #(.width(32)) u__19 (.D(WD), .en(_19en), .Q(_19), .clk(clock), .clr(reset));
  Register #(.width(32)) u__20 (.D(WD), .en(_20en), .Q(_20), .clk(clock), .clr(reset));
  Register #(.width(32)) u__21 (.D(WD), .en(_21en), .Q(_21), .clk(clock), .clr(reset));
  Register #(.width(32)) u__22 (.D(WD), .en(_22en), .Q(_22), .clk(clock), .clr(reset));
  Register #(.width(32)) u__23 (.D(WD), .en(_23en), .Q(_23), .clk(clock), .clr(reset));
  Register #(.width(32)) u__24 (.D(WD), .en(_24en), .Q(_24), .clk(clock), .clr(reset));
  Register #(.width(32)) u__25 (.D(WD), .en(_25en), .Q(_25), .clk(clock), .clr(reset));
  Register #(.width(32)) u__26 (.D(WD), .en(_26en), .Q(_26), .clk(clock), .clr(reset));
  Register #(.width(32)) u__27 (.D(WD), .en(_27en), .Q(_27), .clk(clock), .clr(reset));
  Register #(.width(32)) u__28 (.D(WD), .en(_28en), .Q(_28), .clk(clock), .clr(reset));
  Register #(.width(32)) u__29 (.D(WD), .en(_29en), .Q(_29), .clk(clock), .clr(reset));
  Register #(.width(32)) u__30 (.D(WD), .en(_30en), .Q(_30), .clk(clock), .clr(reset));
  Register #(.width(32)) u__31 (.D(WD), .en(_31en), .Q(_31), .clk(clock), .clr(reset));
  Multiplexer #(.select(5), .width(32), .enable("false")) multiplexer_2 (
    .in0(_0), .in1(_1), .in2(_2), .in3(_3), .in4(_4), .in5(_5), .in6(_6), .in7(_7), .in8(_8), .in9(_9),
    .in10(_10), .in11(_11), .in12(_12), .in13(_13), .in14(_14), .in15(_15), .in16(_16), .in17(_17),
    .in18(_18), .in19(_19), .in20(_20), .in21(_21), .in22(_22), .in23(_23), .in24(_24), .in25(_25),
    .in26(_26), .in27(_27), .in28(_28), .in29(_29), .in30(_30), .in31(_31), .out(RD1), .sel(A1));
  Multiplexer #(.select(5), .width(32), .enable("false")) multiplexer_3 (
    .in0(_0), .in1(_1), .in2(_2), .in3(_3), .in4(_4), .in5(_5), .in6(_6), .in7(_7), .in8(_8), .in9(_9),
    .in10(_10), .in11(_11), .in12(_12), .in13(_13), .in14(_14), .in15(_15), .in16(_16), .in17(_17),
    .in18(_18), .in19(_19), .in20(_20), .in21(_21), .in22(_22), .in23(_23), .in24(_24), .in25(_25),
    .in26(_26), .in27(_27), .in28(_28), .in29(_29), .in30(_30), .in31(_31), .out(RD2), .sel(A2));

  // Other names for the same wires on the sheet: clk = clock; res = reset
endmodule
